# Fritzing sketch main_board (saved by Fritzing 0.7.12b)
breadboards: 1

parts:
  Arduino1 = Arduino
  Part1 = Arduino Xbee Libellium Shield  # not connected
  R1 = Basic Flex Resistor
  R2 = Resistor [tolerance=±5% resistance=1k package=THT]
  M1 = M5450 LED Driver [package="DIP (Dual Inline) [THT]"]
  R3 = Resistor [tolerance=±5% resistance=1k package=THT]
  R4 = Resistor [tolerance=±5% resistance=2.2k package=THT]
  LED1 = white LED - 5mm
  LED2 = white LED - 5mm
  LED3 = white LED - 5mm
  LED4 = white LED - 5mm
  LED5 = white LED - 5mm
  LED6 = white LED - 5mm
  LED7 = white LED - 5mm
  LED8 = white LED - 5mm
  L1 = Solenoid
  Q1 = Basic FET P-Channel [package="TO220 [THT]"]
  D1 = Rectifier Diode [part_number=1N4001 package="300 mil [THT]"]  # not connected

nets:
  N1: Arduino1.D13, M1.out_22
  N2: Arduino1.D11, M1.out_21
  N3: Arduino1.D10, M1.out_24, R3.Pin_1
  N4: Arduino1.D9, M1.out_23
  N5: Arduino1.D7, Q1.source
  N6: Arduino1.D3, M1.out_29
  N7: Arduino1.+5V, R1.Pin_2, M1.out_28, M1.out_26, R3.Pin_0, LED1.cathode, LED2.cathode, LED3.cathode, LED4.cathode, LED5.cathode, LED6.cathode, LED7.cathode, LED8.cathode
  GND: Arduino1.GND, Arduino1.VIN, R2.Pin_0, M1.out_25, M1.out_20, R4.Pin_0, L1.pin1, Q1.gate
  N8: Arduino1.A0, R1.pin_1, R2.Pin_1
  N9: M1.Vss, LED8.anode
  N10: M1.out_17, LED7.anode
  N11: M1.out_16, LED6.anode
  N12: M1.out_15, LED5.anode
  N13: M1.out_14, LED4.anode
  N14: M1.out_13, LED3.anode
  N15: M1.out_12, LED1.anode
  N16: M1.out_11, LED2.anode
  N17: M1.out_27, R4.Pin_1
  N18: L1.pin2, Q1.drain
